# Fritzing sketch Esquema HW 2.0 (saved by Fritzing 0.9.3b)
breadboards: 1

parts:
  M1 = Stepper Motor - Bipolar
  M2 = Stepper Motor - Bipolar
  M3 = Stepper Motor - Bipolar
  M4 = Stepper Motor - Bipolar
  BATT1 = LiPoly Battery (1300mAh)
  BATT2 = LiPoly Battery (1300mAh)
  BATT3 = LiPoly Battery (1300mAh)
  U1 = TRANSCHIPTC5747 [package=camera_sfv24r-2st_2]  # not connected
  Componente1 = Tri-Axis Gyro Breakout - L3G4200D
  Raspberry_Pi_1 = Raspberry Pi 3 [part_number=RPI-3-V1.2]
  Componente2 = Arduino Uno (Rev3)
  USBTTL1 = USB A Plug
  USBTTL2 = Micro USB B Plug
  IC1 = ULN2003A [package="SO16 [SMD]"]
  IC2 = ULN2003A [package="SO16 [SMD]"]
  IC3 = ULN2003A [package="SO16 [SMD]"]
  IC4 = ULN2003A [package="SO16 [SMD]"]

nets:
  N1: M1.A, IC1.Out_3
  N2: M1.C, M2.C, M3.C, M4.C, BATT3.positive, IC1.COM_-_Common, IC2.COM_-_Common, IC3.COM_-_Common, IC4.COM_-_Common
  N3: M1.B, IC1.Out_4
  N4: M1.D, IC1.Out_1
  N5: M2.A, IC2.Out_4
  N6: M2.B, IC2.Out_3
  N7: M2.D, IC2.Out_1
  N8: M3.A, IC3.Out_4
  N9: M3.B, IC3.Out_3
  N10: M3.D, IC3.Out_1
  N11: M4.A, IC4.Out_3
  N12: M4.B, IC4.Out_2
  N13: BATT1.positive, Raspberry_Pi_1.5V
  GND: BATT1.negative, Componente1.GND, Raspberry_Pi_1.GND
  N14: BATT2.positive, Componente2.VIN
  N15: BATT2.negative, Componente2.GND
  N16: BATT3.negative, IC1.0V, IC2.0V, IC3.0V, IC4.0V
  VCC: Componente1.VCC, Raspberry_Pi_1.3v3
  N17: Componente1.SCL, Raspberry_Pi_1.GPIO2
  N18: Componente1.SDA, Raspberry_Pi_1.GPIO3
  N19: Componente2.D8, IC2.In_4
  N20: Componente2.D9_PWM, IC2.In_3
  N21: Componente2.D10_PWM/SS, IC2.In_1
  N22: Componente2.D11_PWM/MOSI, IC1.In_4
  N23: Componente2.D12/MISO, IC1.In_3
  N24: Componente2.D13/SCK, IC1.In_1
  N25: Componente2.D2, IC4.In_4
  N26: Componente2.D3_PWM, IC4.In_3
  N27: Componente2.D4, IC4.In_1
  N28: Componente2.D5_PWM, IC3.In_4
  N29: Componente2.D6_PWM, IC3.In_3
  N30: Componente2.D7, IC3.In_1
  N31: USBTTL1.usb, USBTTL2.usb

custom parts:
  LiPoly Battery (1300mAh): Lithium Ion Polymer Battery (1300mAh)
